# Fritzing sketch rpi3_schematics (saved by Fritzing 0.9.3b)

parts:
  元件1 = Arduino Uno (Rev3)
  DHT1 = DHT11 Humitidy and Temperature Sensor
  Raspberry_Pi_1 = Raspberry Pi 3 [part_number=RPI-3-V1.2]

nets:
  3V3: 元件1.A4/SDA, Raspberry_Pi_1.3v3, Raspberry_Pi_1.GPIO2, Raspberry_Pi_1.3V3
  N1: 元件1.A5/SCL, Raspberry_Pi_1.GPIO3
  N2: 元件1.D7, DHT1.DATA
  5V: 元件1.5V, DHT1.VDD, Raspberry_Pi_1.5V
  GND: 元件1.GND, DHT1.GND, Raspberry_Pi_1.GND

custom parts:
  DHT11 Humitidy and Temperature Sensor: DHT11 Humidity and Temperature Sensor
